# Fritzing sketch Ampelsteuerung (saved by Fritzing 0.9.3b)
circuit board: 8.46667cm x 5.64444cm
breadboards: 1

parts:
  Bauteil1 = Arduino Uno (Rev3)
  Ampel1Taster = Pushbutton [package="[THT]"]
  Ampel2Taster = Pushbutton [package="[THT]"]
  Ampel2Gruen2 = LED - 3mm [color="Green (570nm)" package="3 mm [THT]"]
  Ampel2Rot2 = LED - 3mm [color="Red (633nm)" package="3 mm [THT]"]
  Ampel1Gruen1 = LED - 3mm [color="Green (555nm)" package="3 mm [THT]"]
  Ampel1Rot1 = LED - 3mm [color="Red (633nm)" package="3 mm [THT]"]
  Ampel1Gelb1 = LED - 3mm [color="Yellow (574nm)" package="3 mm [THT]"]
  Ampel1Rot2 = LED - 3mm [color="Red (633nm)" package="3 mm [THT]"]
  Ampel1Gruen2 = LED - 3mm [color="Green (570nm)" package="3 mm [THT]"]
  Ampel2Rot1 = LED - 3mm [color="Red (633nm)" package="3 mm [THT]"]
  Ampel2Gelb1 = LED - 3mm [color="Yellow (595nm)" package="3 mm [THT]"]
  Ampel2Gruen1 = LED - 3mm [color="Green (570nm)" package="3 mm [THT]"]
  R1 = Resistor [tolerance=±5% resistance=150 package=THT]
  R2 = Resistor [tolerance=±5% resistance=150 package=THT]
  R3 = Resistor [tolerance=±5% resistance=150 package=THT]
  R4 = Resistor [tolerance=±5% resistance=150 package=THT]
  R5 = Resistor [tolerance=±5% resistance=150 package=THT]
  R6 = Resistor [tolerance=±5% resistance=150 package=THT]
  R7 = Resistor [tolerance=±5% resistance=150 package=THT]
  R8 = Resistor [tolerance=±5% resistance=150 package=THT]
  R9 = Resistor [tolerance=±5% resistance=150 package=THT]
  R10 = Resistor [tolerance=±5% resistance=150 package=THT]

nets (from the schematic view):
  N1: Bauteil1.D8, R9.Pin_0
  N2: Bauteil1.D9_PWM, R10.Pin_0
  N3: Bauteil1.D12/MISO, Ampel1Taster.Pin_1, Ampel1Taster.Pin_2
  N4: Bauteil1.D13/SCK, Ampel2Taster.Pin_1, Ampel2Taster.Pin_2
  N5: Bauteil1.GND, Ampel2Gruen2.cathode, Ampel2Rot2.cathode, Ampel1Gruen1.cathode, Ampel1Rot1.cathode, Ampel1Gelb1.cathode, Ampel1Rot2.cathode, Ampel1Gruen2.cathode, Ampel2Rot1.cathode, Ampel2Gelb1.cathode, Ampel2Gruen1.cathode
  N6: Bauteil1.D0/RX, R1.Pin_0
  N7: Bauteil1.D1/TX, R2.Pin_0
  N8: Bauteil1.D2, R3.Pin_0
  N9: Bauteil1.D3_PWM, R4.Pin_0
  N10: Bauteil1.D4, R5.Pin_0
  N11: Bauteil1.D5_PWM, R6.Pin_0
  N12: Bauteil1.D6_PWM, R7.Pin_0
  N13: Bauteil1.D7, R8.Pin_0
  N14: Bauteil1.5V, Ampel1Taster.Pin_3, Ampel1Taster.Pin_4, Ampel2Taster.Pin_3, Ampel2Taster.Pin_4
  N15: Ampel2Gruen2.anode, R10.Pin_1
  N16: Ampel2Rot2.anode, R9.Pin_1
  N17: Ampel1Gruen1.anode, R3.Pin_1
  N18: Ampel1Rot1.anode, R1.Pin_1
  N19: Ampel1Gelb1.anode, R2.Pin_1
  N20: Ampel1Rot2.anode, R5.Pin_1
  N21: Ampel1Gruen2.anode, R4.Pin_1
  N22: Ampel2Rot1.anode, R6.Pin_1
  N23: Ampel2Gelb1.anode, R7.Pin_1
  N24: Ampel2Gruen1.anode, R8.Pin_1

// code stored in the sketch: Ampelsteuerung.ino
int ampel1red1 = 0;
int ampel1yellow1 = 1;
int ampel1green1 = 2;
#define ampel1red2  3;
#define ampel1green2 4
#define ampel2red1 5
#define ampel2yellow1 6
int ampel2green1 = 7;
int ampel2red2 = 8;
int ampel2green2 = 9;
int ampel1Taster = 12;
int ampel2Taster = 13;


void setup(){
	pinMode(ampel1red1,OUTPUT);
	pinMode(ampel1yellow1,OUTPUT);
	pinMode(ampel1green1,OUTPUT);
	pinMode(ampel1red2,OUTPUT);
	pinMode(ampel1green2,OUTPUT);
	pinMode(ampel2red1,OUTPUT);
	pinMode(ampel2yellow1,OUTPUT);
	pinMode(ampel2green1,OUTPUT);
	pinMode(ampel2red2,OUTPUT);
	pinMode(ampel2green2,OUTPUT);
	pinMode(ampel1Taster,INPUT);
	pinMode(ampel2Taster,INPUT);
}

void loop(){
	
}

// code stored in the sketch: Ampelsteuerung2.ino.ino
// Each constant contains the index of PINS
enum MAP{ AMPEL1RED1,
          AMPEL1YELLOW1,
          AMPEL1GREEN1,
          AMPEL1RED2,
          AMPEL1GREEN2,
          AMPEL2RED1,
          AMPEL2YELLOW1,
          AMPEL2GREEN1,
          AMPEL2RED2,
          AMPEL2GREEN2,
          AMPEL1TASTER,
          AMPEL1TASTERRESET,
          AMPEL2TASTER,
          AMPEL2TASTERRESET
       };

// Array with the used pinnumbers
// Which Pin is what constant is in the enum MAP          
const int PINS[] = {0,1,2,3,4,5,6,7,8,9,10,12,11,13};

void setup() {
  pinMode(PINS[AMPEL1RED1], OUTPUT);
  pinMode(PINS[AMPEL1YELLOW1], OUTPUT);
  pinMode(PINS[AMPEL1GREEN1], OUTPUT);
  pinMode(PINS[AMPEL1RED2], OUTPUT);
  pinMode(PINS[AMPEL1GREEN2], OUTPUT);
  pinMode(PINS[AMPEL2RED1], OUTPUT);
  pinMode(PINS[AMPEL2YELLOW1], OUTPUT);
  pinMode(PINS[AMPEL2GREEN1], OUTPUT);
  pinMode(PINS[AMPEL2RED2], OUTPUT);
  pinMode(PINS[AMPEL2GREEN2], OUTPUT);
  pinMode(PINS[AMPEL1TASTERRESET],OUTPUT);
  pinMode(PINS[AMPEL1TASTER], INPUT);
  pinMode(PINS[AMPEL2TASTERRESET],OUTPUT);
  pinMode(PINS[AMPEL2TASTER], INPUT);

  int outputval = 0;
  outputval += getAddValue(true,AMPEL1GREEN1);
  outputval += getAddValue(true,AMPEL1RED2);
  outputval += getAddValue(true,AMPEL2RED1);
  outputval += getAddValue(true,AMPEL2RED2);
  output(outputval);
  
  Serial.begin(9600);
}

void loop() {
  boolean nightmode = false;
  int input = getInput();
	Serial.println("Hallo");
  int ret = 0;
  if(nightmode){
    ret = runnightmode(input);
  }else{
    ret = runstandardmode(input);
  }
  output(ret);
  delay(500);
}

int runstandardmode(int input){
  boolean stp0 = true,stp1 = false,stp2 = false,stp3 = false,stp4 = false,stp5 = false,stp6 = false,stp7 = false;

  boolean taster1 = mask(input,AMPEL1TASTER);
  boolean taster2 = mask(input,AMPEL2TASTER);
  
  if(stp7 && mask(input,AMPEL1YELLOW1) &&
            mask(input,AMPEL1RED1) &&
            mask(input,AMPEL2RED1)){
    stp7 = false;
    stp0 = true;
  }
  
  if(stp0 && mask(input, AMPEL1GREEN1) &&
            mask(input, AMPEL2RED1) ){
    stp0 = false;
    stp1 = true;
  }

  if(stp1 && mask(input,AMPEL1YELLOW1) &&
            mask(input,AMPEL2RED2) ){
    stp1 = false;
    stp2 = true;
  }

  if(stp2 && mask(input,AMPEL1RED1) &&
            mask(input,AMPEL2RED1) ){
    stp2 = false;
    stp3 = true;
  }

  if(stp3 && mask(input,AMPEL1RED1) &&
            mask(input,AMPEL2YELLOW1) &&
            mask(input,AMPEL2RED1) ){
    stp3 = false;
    stp4 = true;
  }

  if(stp4 && mask(input,AMPEL1RED1) &&
            mask(input,AMPEL2GREEN1)){
    stp4 = false;
    stp5 = true;            
  }

  if(stp5 && mask(input,AMPEL1RED1) &&
            mask(input,AMPEL2YELLOW1)){
    stp5 = false;
    stp6 = true;
  }

  if(stp6 && mask(input,AMPEL1RED1)&&
            mask(input,AMPEL2RED1)){
    stp6 = false;
    stp7 = true;
  }

  int outputval = 0;
  outputval += getAddValue(stp0,AMPEL1GREEN1);
  outputval += getAddValue(stp1||stp7,AMPEL1YELLOW1);
  outputval += getAddValue(!stp0&&!stp1,AMPEL1RED1);
  outputval += getAddValue(stp0 && taster1,AMPEL1GREEN2);
  outputval += getAddValue(!(stp0 && taster1),AMPEL1RED2);
  outputval += getAddValue(stp4,AMPEL2GREEN1);
  outputval += getAddValue(stp3||stp5,AMPEL2YELLOW1);
  outputval += getAddValue(!stp4&&!stp5,AMPEL2RED1);
  outputval += getAddValue(stp4&&taster2,AMPEL2GREEN2);
  outputval += getAddValue(!(stp4&&taster2),AMPEL2RED2);

  if(!(stp0 && taster1)) resetFF(AMPEL1TASTERRESET);
  if(!(stp4 && taster2)) resetFF(AMPEL2TASTERRESET);
  //output(outputval);
  return outputval;
}

int runnightmode(int input){
  return getAddValue(!mask(input,AMPEL2YELLOW1),AMPEL2YELLOW1);
}


int getInput() {
  int ret = 0;
  for(int i = 0; i < arrayLength(PINS);i++){
    ret += readDPin(PINS[i]) * pow(2,PINS[i]);
  }
  return ret;
}

void resetFF(MAP m){
  writeMDPin(m,HIGH);
  writeMDPin(m,LOW);
}

void output(int outVal) {
  int max = arrayLength(PINS);
  for(int i = 0;i < max;i++){
    writeDPin(PINS[i],mask(outVal,PINS[i]) ? HIGH : LOW);
  }
}

/*
 * Berechne arraylänge
 */
int arrayLength(int a[]){
  return sizeof(a)/sizeof(a[0]);
}

/*
 * Es wird der Pin des gemappten Wert m in input ausmaskiert und dann geprüft ob der Wert true ist
 */ 
boolean mask(int input, MAP m){
  return mask(input,getMPin(m));
}

boolean mask(int input, int p){
  return (input & int(pow(2, p))) == true;
}

/* 
 *  Gibt den zu addieren Wert zurück wenn b true ist sonst 0
 */
int getAddValue(boolean b, MAP m){
  if(b){
    return pow(2,getMPin(m));
  }else{
    return 0;
  }
}

// Pinnummer des gemappten Wertes
int getMPin(MAP m){
  return PINS[m];
}

// k = Pinnummer
int readDPin(int k){
  return digitalRead(k);
}

/*  k = Pinnummer
 *  v = 1 oder 0
 */ 
void writeDPin(int k, int v){
  digitalWrite(k,v);
}

// k = Wert aus MAP
int readMDPin(MAP k){
  return readDPin(PINS[k]);
}
/*  k = Wert aus MAP
 *  v = 1 oder 0
 */
void writeMDPin(MAP k, int v){
  digitalWrite(PINS[k],v);
}
